# Fritzing sketch Frotect (saved by Fritzing 0.8.3b)
breadboards: 1

parts:
  LED1 = LED - 5mm [color="Red (633nm)" package="5 mm [THT]"]
  R1 = Resistor [tolerance=±5% resistance=220 package="1206 [SMD]"]
  Bauteil1 = Bluetooth Mate Silver  # not connected
  R2 = Resistor [tolerance=±5% resistance=4.7k package=THT]
  T2 = LM34 Temperature Sensor [package="TO92 [THT]"]
  T3 = LM34 Temperature Sensor [package="TO92 [THT]"]
  T4 = LM34 Temperature Sensor [package="TO92 [THT]"]
  T5 = LM34 Temperature Sensor [package="TO92 [THT]"]
  Arduino1 = Arduino Mini (Rev5)
  S1 = SWITCH-MOMENTARY-2 [package=reed_switch_plastic]
  JP1 = Header 2 [package=screwterminal-3.5mm-2_lock]
  JP2 = Header 2 [package=screwterminal-3.5mm-2_lock]
  JP3 = Header 2 [package=screwterminal-3.5mm-2_lock]
  JP4 = Header 2 [package=screwterminal-3.5mm-2_lock]
  JP5 = Header 2 [package=screwterminal-3.5mm-2_lock]
  PCB2 = 4CH RELAY BOARD [package=relay-g5q]
  J1 = Screw terminal - 2 pins [package=THT]

nets:
  N1: LED1.cathode, Arduino1.D11_PWM
  N2: LED1.anode, R1.Pin_1
  VCC: R1.Pin_0, R2.Pin_1, T2.Vcc, T3.Vcc, T4.Vcc, T5.Vcc, Arduino1.5V, PCB2.VCC, J1.pin2
  N3: R2.Pin_0, T2.DQ, T3.DQ, T4.DQ, T5.DQ
  GND: T2.GND, T3.GND, T4.GND, T5.GND, Arduino1.GND, S1.1, PCB2.GND, PCB2.GND2, J1.pin1
  N4: Arduino1.RESET, Arduino1.D10_PWM, S1.2
  N5: Arduino1.D2, PCB2.IN4
  N6: Arduino1.D4, PCB2.IN3
  N7: Arduino1.D5_PWM, PCB2.IN2
  N8: Arduino1.D6_PWM, PCB2.IN1
  N9: JP1.1, PCB2.COM1
  N10: JP1.2, JP2.2, JP3.2, JP4.2, JP5.1
  N11: JP2.1, PCB2.COM2
  N12: JP3.1, PCB2.COM3
  N13: JP4.1, PCB2.COM4
  N14: JP5.2, PCB2.connector11, PCB2.connector12, PCB2.connector13, PCB2.connector14

notes:
  AC Input
  AC output
  strand 1-4
  HC-05
  bluetooth module
  confgured to
  57600 baud.
  power
  supply
  5V
  heartbeat indicator

custom parts:
  Bluetooth Mate Silver: Description: The Bluetooth Mate is very similar to our BlueSMiRF modem, but it is designed specifically to be used with our Arduino Pros and LilyPad Arduinos. These modems work as a serial (RX/TX) pipe, and are a great wireless replacement for serial cables. Any serial stream from 9600 to 115200bps can be passed seamlessly from your computer to your target. Bluetooth Mate has the same pin out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
  LM34 Temperature Sensor: Dallas DS18B20
  4CH RELAY BOARD: Sainsmart 4Channels, 5V Solid state relay board
